# Fritzing sketch Schematic (saved by Fritzing 0.9.2b)

parts:
  U1 = RELAY-SOLIDSTATE [package=relay-s108t02]
  LED1 = LEDs [package=led10mm]
  S1 = Round Pushbutton
  R1 = Resistor [tolerance=±5% resistance=10k package="0402 [SMD]"]
  R2 = Resistor [tolerance=±5% resistance=1k package="1206 [SMD]"]
  Raspberry_Pi1 = Raspberry Pi B+
  PIR1 = PIR sensor
  J1 = Piezo Speaker

nets:
  N1: U1.T1, LED1.C
  GND: U1.T2, U1.-, S1.leg0, Raspberry_Pi1.GND, PIR1.GND, J1.pin1
  N2: U1.+, Raspberry_Pi1.GPIO4
  5V: LED1.A, Raspberry_Pi1.5V, PIR1.VDD
  N3: S1.leg1, R1.Pin_1, R2.Pin_1
  3V3: R1.Pin_0, Raspberry_Pi1.3v3, Raspberry_Pi1.3V3
  N4: R2.Pin_0, Raspberry_Pi1.GPIO27
  N5: Raspberry_Pi1.GPIO2, J1.pin2
  N6: Raspberry_Pi1.GPIO17, PIR1.SIG
